// Digital circuit Divisor8bits.dig as structural Verilog
module Divisor8bits (
  input  [7:0] A,
  input  [7:0] B,
  input  clk
);

  wire multiplexer_1_out;

  Multiplexer multiplexer_1 (.in_0(A[0]), .out(multiplexer_1_out));  // open: sel, in_1
  Register N_div (.D(multiplexer_1_out));  // open: C, en, Q
  Register N_Guardado ();  // open: D, C, en, Q
  // Pins of 1 and 8 bits meet at A
endmodule
